# Fritzing sketch RPi.PIR (saved by Fritzing 0.9.2b)

parts:
  Raspberry_Pi_B_rev1 = Raspberry Pi B rev1
  PIR1 = PIR sensor

nets:
  3V3: Raspberry_Pi_B_rev1.3V3, PIR1.VDD
  GND: Raspberry_Pi_B_rev1.GND, PIR1.GND
  N1: Raspberry_Pi_B_rev1.GPIO_4, PIR1.SIG
